# Fritzing sketch Untitled Sketch (saved by Fritzing 1.0.2b)
breadboards: 1

parts:
  A1 = Particle - Photon2
  Grove1 = Grove Dust Sensor  # not connected
  SENS1 = SoilWatch 10  # not connected
  Part1 = MQ-131 breakout  # not connected
  R1 = Resistor [tolerance=±5% power=0.25W resistance=2.2k package=THT]
  R2 = Resistor [tolerance=±5% power=0.25W resistance=220 package=THT]
  Q1 = PNP-Transistor [package="TO92 [THT]"]
  Relay1 = Relay - 6 pins [package="DIP (Dual Inline) [THT]"]
  M1 = DC Motor [voltage_(max)=6V voltage_(min)=3V]

nets:
  N1: A1.Pin_2, A1.Pin_31, Relay1.VCC
  N2: A1.Pin_4, A1.Pin_30, R1.Pin_0, Q1.C, Relay1.GND, M1.pin_2
  N3: A1.Pin_13, R1.Pin_1, Q1.B
  N4: A1.Pin_26, R2.Pin_0, Relay1.ON
  N5: R2.Pin_1, Q1.E, Relay1.IN
  N6: Relay1.COM, M1.pin_1

custom parts:
  Particle - Photon2: The Photon 2 is a microcontroller and Wi-Fi networking developed by particle. Features: 802.11a/b/g/n Wi-Fi, 2.4 GHz and 5 GHz Integrated PCB antenna Integrated U.FL connector for external antenna Integrated RF switch BLE 5 using same antenna as Wi-Fi Realtek RTL8721DM MCU ARM Cortex M33 CPU, 200 MHz 2048 KB (2 MB) user application maximum size 3072 KB (3 MB) of RAM available to user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
  Grove Dust Sensor: PPD42 Grove Dust Sensor
  SoilWatch 10: SoilWatch 10 - Capacitive soil moisture sensor
  MQ-131 breakout: SKU: 101282
  Relay - 6 pins: A DIP stand-in part for whatever IC you want. With 6 pins on a 900mil dual inline package (DIP) footprint.
